// Logisim project SOMADOR.circ as structural Verilog: 4 circuits, main circuit somador
module somador (
  input  A,
  input  B,
  output S,
  output CO
);

  xor xor_1 (S, A, B);
  and and_1 (CO, A, B);
endmodule

module somador_completo (
  input  CI,
  input  A,
  input  B,
  output S,
  output CO
);

  wire somador_1_co, somador_1_s, somador_2_co;

  somador somador_1 (.A(A), .B(B), .S(somador_1_s), .CO(somador_1_co));
  somador somador_2 (.A(CI), .B(somador_1_s), .S(S), .CO(somador_2_co));
  or or_1 (CO, somador_2_co, somador_1_co);
endmodule

module somador_de_4_bits (
  input  C0,
  input  A0,
  input  B0,
  input  A1,
  input  B1,
  input  A2,
  input  B2,
  input  A3,
  input  B3,
  output S0,
  output S1,
  output S2,
  output S3,
  output C4
);

  wire somador_completo_1_co, somador_completo_2_co, somador_completo_3_co;

  somador_completo somador_completo_1 (.CI(C0), .A(A0), .B(B0), .S(S0), .CO(somador_completo_1_co));
  somador_completo somador_completo_2 (.CI(somador_completo_1_co), .A(A1), .B(B1), .S(S1), .CO(somador_completo_2_co));
  somador_completo somador_completo_3 (.CI(somador_completo_2_co), .A(A2), .B(B2), .S(S2), .CO(somador_completo_3_co));
  somador_completo somador_completo_4 (.CI(somador_completo_3_co), .A(A3), .B(B3), .S(S3), .CO(C4));
endmodule

module somador_de_8_bits (
  input  C0,
  input  A0,
  input  B0,
  input  A1,
  input  B1,
  input  A2,
  input  B2,
  input  A3,
  input  B3,
  input  A4,
  input  B4,
  input  A5,
  input  B5,
  input  A6,
  input  B6,
  input  A7,
  input  B7,
  output S0,
  output S1,
  output S2,
  output S3,
  output S4,
  output S5,
  output S6,
  output S7,
  output C8
);

  wire somador_de_4_bits_1_c4;

  somador_de_4_bits somador_de_4_bits_1 (
    .C0(C0), .A0(A0), .B0(B0), .A1(A1), .B1(B1), .A2(A2), .B2(B2), .A3(A3), .B3(B3), .S0(S0), .S1(S1),
    .S2(S2), .S3(S3), .C4(somador_de_4_bits_1_c4));
  somador_de_4_bits somador_de_4_bits_2 (
    .C0(somador_de_4_bits_1_c4), .A0(A4), .B0(B4), .A1(A5), .B1(B5), .A2(A6), .B2(B6), .A3(A7), .B3(B7),
    .S0(S4), .S1(S5), .S2(S6), .S3(S7), .C4(C8));
endmodule
